// Logisim project Detector_Gas_Completo.circ as structural Verilog: 1 circuit, main circuit main
module main (
  input  POR,
  input  RESET,
  input  GAS,
  input  ARMAR
);

  wire and_1_out, and_2_out, nor_1_out, nor_2_out, or_1_out;

  or or_1 (or_1_out, POR, RESET);
  and and_1 (and_1_out, GAS, ARMAR);
  LED led_1 (.in(ARMAR));
  nor nor_1 (nor_1_out, or_1_out, nor_2_out);
  nor nor_2 (nor_2_out, nor_1_out, and_1_out);
  and and_2 (and_2_out, nor_2_out, ARMAR);
  LED led_2 (.in(and_2_out));
  LED led_3 (.in(nor_1_out));
  LED led_4 (.in(nor_1_out));
  LED led_5 (.in(nor_1_out));

  // Notes on the sheet:
  //   GUIA DE OPERACAO:
  //   1. Acione POR (P=1) e solte (P=0) - inicializa o sistema
  //   2. Acione ARMAR (A=1) - LED amarelo + verde acendem
  //   3. Acione GAS (G=1) - LEDs vermelho, laranja e branco acendem
  //   4. Desligue GAS (G=0) - alarme PERMANECE ativo (memoria!)
  //   5. Acione RESET (R=1) - sistema retorna a vigilancia
  //   OR (R+P)
  //   AND (G.A)
  //   AMARELO
  //   (Sistema Armado)
  //   DETECTOR DE VAZAMENTO DE GAS - VERSAO COMPLETA
  //   NOR-Q 1
  //   NOR-Q 2
  //   AND (~Q.A)
  //   VERMELHO
  //   (Alarme)
  //   LARANJA
  //   (Buzzer)
  //   BRANCO
  //   (Exaustor)
  //   VERDE
  //   (Vigilancia OK)
endmodule
