// Logisim project Latch_SR_INTERMEDIARIO - Entregavel 2.circ as structural Verilog: 1 circuit, main circuit main
module main (
  input  SENSOR,
  input  RESET
);

  wire nor_1_out, nor_2_out, not_1_out;

  not not_1 (not_1_out, SENSOR);
  nor nor_1 (nor_1_out, not_1_out, nor_2_out);
  nor nor_2 (nor_2_out, nor_1_out, RESET);
  LED led_1 (.in(nor_1_out));
  LED led_2 (.in(nor_2_out));
  LED led_3 (.in(nor_2_out));

  // Notes on the sheet:
  //   (Reed Switch)
  //   (Push-button)
  //   +5V (VCC)
  //   alimentação
  //   INVERSOR
  //   (74LS04)
  //   GND
  //   terra
  //   📋 COMO USAR (sequência correta):
  //   1. Clique em SENSOR (vai para 1) → simula 'porta fechada' (reed switch ativo)
  //   2. Clique em RESET (vai para 1) e depois solte → inicializa o sistema (LED VERDE acende)
  //   3. Clique em SENSOR de volta para 0 → simula 'porta aberta' → LED VERMELHO + BUZZER acionam!
  //   4. Clique em SENSOR para 1 novamente → ALARME continua ativo (MEMÓRIA do Latch SR!)
  //   5. Clique em RESET para silenciar o alarme
  //   NOR 1
  //   NOR 2 (74LS02)
  //   ALARME DIGITAL COM LATCH SR - VERSÃO INTERMEDIÁRIA
  //   EECP0002 - Circuitos Digitais | Apresentação Prévia
  //   LED VERDE
  //   ✓ Sistema Normal
  //   LED VERMELHO
  //   🚨 ALARME ATIVO
  //   BUZZER
  //   🔊 Piezoelétrico 5V
  //   📦 COMPONENTES:
  //   • Inversor: CI 74LS04
  //   • Latch SR: CI 74LS02 (NOR)
  //   • Sensor: Reed Switch + Ímã
  //   • Reset: Push-button NA
  //   • Buzzer: Piezoelétrico 5V
  //   • LEDs: 5mm + R330Ω
  //   • Resistores pull-down: 10kΩ
  //   • Alimentação: 5V (USB ou pilhas)
  //   📊 TABELA VERDADE:
  //   S R | Q ~Q | Estado
  //   0 0 | Q ~Q | MEMÓRIA
  //   1 0 | 1  0 | SET (Alarme ON)
  //   0 1 | 0  1 | RESET (Alarme OFF)
  //   1 1 | 0  0 | PROIBIDO
endmodule
